# Fritzing sketch a9g-puddin-board 2 (saved by Fritzing 0.9.3b)
circuit board: 5.62017cm x 6.00642cm
breadboards: 1

parts:
  J6 = female pin header, 16 pins [form="♀ (female)"]
  J9 = Generic female header - 6 pins [form="♀ (female)" package=THT]
  SW1 = DIP Switch 8 Position [package=dipswitch-08]
  J10 = Generic female header - 16 pins [form="♀ (female)" package=THT]

nets:
  N1: J6.pin1, J9.GND
  N2: J9.RTI, SW1.11, SW1.13, SW1.15
  N3: J9.5V, SW1.9
  N4: SW1.2, J10.TX1
  N5: SW1.3, J10.RX1
  N6: SW1.4, J10.GPS_TX
  N7: SW1.5, J10.GPS_RX
  N8: SW1.6, J10.HST_TX
  N9: SW1.7, J10.HST_RX

notes:
  5V
  HST
  GPS
  UART
  5
  G
  T
  R
  D
  3

custom parts:
  Generic female header - 6 pins: Generic female header
  Generic female header - 16 pins: Generic female header
